// Logisim project Projet2.circ as structural Verilog: 5 circuits, main circuit main
module main (
);

  wire d_ff_1_q, random_mode_1_exit, Reset, SettingExit;
  wire [3:0] demultiplexer_1_out0, demultiplexer_1_out1, N_out;
  wire [6:0] display_mode_1_out_7, display_mode_1_out_8, display_mode_1_out_9, display_mode_1_out_10,
       random_mode_1__1st, random_mode_1__2nd, random_mode_1__3rd, setting_mode_1_num;

  Button N (.out(N_out[0]));
  Button P1 (.out(N_out[1]));
  Button P2 (.out(N_out[2]));
  Button P3 (.out(N_out[3]));
  Demultiplexer #(.width(4)) demultiplexer_1 (
    .out0(demultiplexer_1_out0), .out1(demultiplexer_1_out1), .in(N_out), .sel(d_ff_1_q));  // open: en
  D_Flip_Flop #(.trigger("falling")) d_ff_1 (
    .Q(d_ff_1_q), .preset(SettingExit), .reset(Reset));  // open: clk, D, Qn, en
  Setting_mode setting_mode_1 (
    .Reset(Reset), .N(demultiplexer_1_out0[0]), .P1(demultiplexer_1_out0[1]), .P2(demultiplexer_1_out0[2]),
    .P3(demultiplexer_1_out0[3]), .Num(setting_mode_1_num), .Exit(SettingExit));
  Random_mode random_mode_1 (
    .Reset(Reset), .P1(demultiplexer_1_out1[1]), .P2(demultiplexer_1_out1[2]), .P3(demultiplexer_1_out1[3]),
    ._1st(random_mode_1__1st), .Exit(random_mode_1_exit), ._2nd(random_mode_1__2nd),
    ._3rd(random_mode_1__3rd), .N(demultiplexer_1_out1[0]));
  Display_mode display_mode_1 (
    .in_1(setting_mode_1_num), .in_2(random_mode_1__1st), .in_3(random_mode_1__2nd),
    .in_4(random_mode_1__3rd), .P2(demultiplexer_1_out1), .out_7(display_mode_1_out_7),
    .out_8(display_mode_1_out_8), .out_9(display_mode_1_out_9), .out_10(display_mode_1_out_10),
    .Reset(Reset), .Enter(random_mode_1_exit));
  _7_Segment_Display u_7_segment_display_1 (
    .g(display_mode_1_out_7[6]), .f(display_mode_1_out_7[5]), .a(display_mode_1_out_7[4]),
    .b(display_mode_1_out_7[3]), .e(display_mode_1_out_7[2]), .d(display_mode_1_out_7[1]),
    .c(display_mode_1_out_7[0]));  // open: dp
  _7_Segment_Display u_7_segment_display_2 (
    .g(display_mode_1_out_8[6]), .f(display_mode_1_out_8[5]), .a(display_mode_1_out_8[4]),
    .b(display_mode_1_out_8[3]), .e(display_mode_1_out_8[2]), .d(display_mode_1_out_8[1]),
    .c(display_mode_1_out_8[0]));  // open: dp
  _7_Segment_Display u_7_segment_display_3 (
    .g(display_mode_1_out_9[6]), .f(display_mode_1_out_9[5]), .a(display_mode_1_out_9[4]),
    .b(display_mode_1_out_9[3]), .e(display_mode_1_out_9[2]), .d(display_mode_1_out_9[1]),
    .c(display_mode_1_out_9[0]));  // open: dp
  _7_Segment_Display u_7_segment_display_4 (
    .g(display_mode_1_out_10[6]), .f(display_mode_1_out_10[5]), .a(display_mode_1_out_10[4]),
    .b(display_mode_1_out_10[3]), .e(display_mode_1_out_10[2]), .d(display_mode_1_out_10[1]),
    .c(display_mode_1_out_10[0]));  // open: dp

  // Notes on the sheet:
  //   Random mode
  //   Setting mode
  //   Display mode
  //   Num
  //   1st
  //   2nd
  //   3rd
endmodule

module Setting_mode (
  input  Reset,
  input  N,
  input  P1,
  input  P2,
  input  P3,
  output [6:0] Num,
  output Exit
);

  wire and_1_out, and_2_out, and_4_out, clock_1_out, clock_2_out, comparator_1_eq, counter_1_carry,
       d_ff_1_qn, d_ff_2_qn, not_1_out, not_2_out, OK3SEC, or_1_out, or_2_out, or_3_out, or_4_out;
  wire [1:0] and_5_out;
  wire [2:0] counter_2_q;
  wire [3:0] counter_1_q;
  wire [6:0] hexa_to_7seg_1__7seg;

  Counter #(.width(4), .max('ha)) counter_1 (
    .count(and_1_out), .Q(counter_1_q), .carry(counter_1_carry), .clk(and_1_out), .clr(or_1_out));  // open: load, D
  or or_1 (or_1_out, Reset, counter_1_carry);
  and and_1 (and_1_out, OK3SEC, N);
  or or_2 (or_2_out, N, P1, P2, P3);
  or or_3 (or_3_out, P1, P2, P3);
  Counter #(.width(3), .max('h7)) counter_2 (
    .count(or_2_out), .Q(counter_2_q), .clk(clock_1_out), .clr(or_4_out));  // open: load, D, carry
  or or_4 (or_4_out, and_2_out, Exit);
  Clock #(.highDuration(4), .lowDuration(4)) clock_1 (.out(clock_1_out));
  and and_2 (and_2_out, not_1_out, d_ff_2_qn);
  not not_1 (not_1_out, or_2_out);
  hexa_to_7seg hexa_to_7seg_1 (.Hexa(counter_1_q), ._7seg(hexa_to_7seg_1__7seg));
  Clock #(.highDuration(4), .lowDuration(4)) clock_2 (.out(clock_2_out));
  D_Flip_Flop d_ff_1 (.Q(and_5_out[1]), .Qn(d_ff_1_qn), .preset(and_1_out), .reset(Reset));  // open: clk, D, en
  and and_3 (Exit, and_5_out[1], or_3_out);
  not not_2 (not_2_out, OK3SEC);
  and and_4 (and_4_out, not_2_out, comparator_1_eq);
  Comparator #(.width(3)) comparator_1 (.a(3'b011), .b(counter_2_q), .eq(comparator_1_eq));  // open: gt, lt
  Multiplexer #(.select(2), .width(7)) multiplexer_1 (
    .in0({7{1'b0}}), .in1(7'b0111111), .in2(hexa_to_7seg_1__7seg), .out(Num), .sel(and_5_out));  // open: in3, en
  and and_5 (and_5_out[0], clock_2_out, d_ff_1_qn, OK3SEC);
  D_Flip_Flop #(.trigger("falling")) d_ff_2 (
    .Q(OK3SEC), .Qn(d_ff_2_qn), .preset(and_4_out), .reset(Reset));  // open: clk, D, en

  // Other names for the same wires on the sheet: CLR = Reset
endmodule

module hexa_to_7seg (
  input  [3:0] Hexa,
  output [6:0] _7seg
);

  Multiplexer #(.select(4), .width(7)) multiplexer_1 (
    .in0(7'b0111111), .in1(7'b0001001), .in2(7'b1011110), .in3(7'b1011011), .in4(7'b1101001),
    .in5(7'b1110011), .in6(7'b1110111), .in7(7'b0011001), .in8({7{1'b1}}), .in9(7'b1111011),
    .in10({7{1'b0}}), .out(_7seg), .sel(Hexa));  // open: in11, in12, in13, in14, in15, en
endmodule

module Random_mode (
  input  Reset,
  input  N,
  input  P1,
  input  P2,
  input  P3,
  output [6:0] _1st,
  output [6:0] _2nd,
  output Exit,
  output [6:0] _3rd
);

  wire and_1_out, and_2_out, and_3_out, and_4_out, and_5_out, and_6_out, and_7_out, and_8_out, and_9_out,
       clock_1_out, clock_2_out, clock_3_out, clock_4_out, clock_5_out, clock_6_out, clock_7_out,
       clock_8_out, clock_9_out, comparator_1_gt, comparator_2_gt, comparator_3_gt, d_ff_1_q, d_ff_2_q,
       d_ff_3_q, d_ff_4_q, d_ff_5_q, d_ff_6_q, multiplexer_1_out, multiplexer_2_out, multiplexer_3_out,
       not_1_out, not_2_out, not_3_out, not_4_out, not_5_out, not_6_out, OKP1, OKP2, OKP3, or_1_out,
       or_2_out, or_3_out;
  wire [3:0] counter_1_q, counter_2_q, counter_3_q;
  wire [6:0] hexa_to_7seg_1__7seg, hexa_to_7seg_2__7seg, hexa_to_7seg_3__7seg;
  wire [7:0] divider_1_out, divider_2_out, divider_3_out, random_1_out, random_2_out, random_3_out;

  Clock #(.highDuration(4), .lowDuration(4)) clock_1 (.out(clock_1_out));
  Clock clock_2 (.out(clock_2_out));
  and and_1 (and_1_out, P3, not_1_out);
  not not_1 (not_1_out, d_ff_2_q);
  Clock #(.highDuration(4), .lowDuration(4)) clock_3 (.out(clock_3_out));
  Clock clock_4 (.out(clock_4_out));
  Clock #(.highDuration(4), .lowDuration(4)) clock_5 (.out(clock_5_out));
  Clock clock_6 (.out(clock_6_out));
  and and_2 (and_2_out, P2, not_2_out);
  and and_3 (and_3_out, comparator_3_gt, d_ff_1_q);
  not not_2 (not_2_out, d_ff_1_q);
  D_Flip_Flop #(.trigger("falling")) d_ff_1 (.clk(P2), .D(1'b1), .Q(d_ff_1_q), .reset(Reset));  // open: Qn, preset, en
  Multiplexer multiplexer_1 (
    .in0(clock_1_out), .in1(clock_2_out), .out(multiplexer_1_out), .sel(not_3_out));  // open: en
  or or_1 (or_1_out, and_1_out, and_4_out);
  not not_3 (not_3_out, d_ff_2_q);
  and and_4 (and_4_out, comparator_1_gt, d_ff_2_q);
  D_Flip_Flop #(.trigger("falling")) d_ff_2 (.clk(P3), .D(1'b1), .Q(d_ff_2_q), .reset(Reset));  // open: Qn, preset, en
  Multiplexer multiplexer_2 (
    .in0(clock_3_out), .in1(clock_4_out), .out(multiplexer_2_out), .sel(not_4_out));  // open: en
  and and_5 (and_5_out, P1, not_5_out);
  or or_2 (or_2_out, and_5_out, and_6_out);
  not not_4 (not_4_out, d_ff_3_q);
  and and_6 (and_6_out, comparator_2_gt, d_ff_3_q);
  not not_5 (not_5_out, d_ff_3_q);
  D_Flip_Flop #(.trigger("falling")) d_ff_3 (.clk(P1), .D(1'b1), .Q(d_ff_3_q), .reset(Reset));  // open: Qn, preset, en
  Multiplexer multiplexer_3 (
    .in0(clock_5_out), .in1(clock_6_out), .out(multiplexer_3_out), .sel(not_6_out));  // open: en
  Random #(.seed(595959)) random_1 (.clk(multiplexer_3_out), .next(or_3_out), .out(random_1_out));  // open: clr
  or or_3 (or_3_out, and_2_out, and_3_out);
  not not_6 (not_6_out, d_ff_1_q);
  Random #(.seed(39291)) random_2 (.clk(multiplexer_1_out), .next(or_1_out), .out(random_2_out));  // open: clr
  Counter #(.width(4), .max('hf)) counter_1 (
    .count(and_7_out), .Q(counter_1_q), .clk(clock_7_out), .clr(Reset));  // open: load, D, carry
  and and_7 (and_7_out, comparator_1_gt, d_ff_2_q);
  Clock #(.highDuration(4), .lowDuration(4)) clock_7 (.out(clock_7_out));
  Random #(.seed(747429)) random_3 (.clk(multiplexer_2_out), .next(or_2_out), .out(random_3_out));  // open: clr
  and and_8 (and_8_out, comparator_2_gt, d_ff_3_q);
  Clock #(.highDuration(4), .lowDuration(4)) clock_8 (.out(clock_8_out));
  Divider divider_1 (.a(random_1_out), .b(8'h1a), .out(divider_1_out));  // open: upper, rem
  Counter #(.width(4), .max('hf)) counter_2 (
    .count(and_9_out), .Q(counter_2_q), .clk(clock_9_out), .clr(Reset));  // open: load, D, carry
  and and_9 (and_9_out, comparator_3_gt, d_ff_1_q);
  Clock #(.highDuration(4), .lowDuration(4)) clock_9 (.out(clock_9_out));
  Divider divider_2 (.a(random_2_out), .b(8'h1a), .out(divider_2_out));  // open: upper, rem
  Comparator #(.width(4)) comparator_1 (.a(4'b0100), .b(counter_1_q), .gt(comparator_1_gt), .eq(OKP3));  // open: lt
  Divider divider_3 (.a(random_3_out), .b(8'h1a), .out(divider_3_out));  // open: upper, rem
  Comparator #(.width(4)) comparator_2 (.a(4'b0100), .b(counter_3_q), .gt(comparator_2_gt), .eq(OKP1));  // open: lt
  Counter #(.width(4), .max('hf)) counter_3 (
    .count(and_8_out), .Q(counter_3_q), .clk(clock_8_out), .clr(Reset));  // open: load, D, carry
  Comparator #(.width(4)) comparator_3 (.a(4'b0100), .b(counter_2_q), .gt(comparator_3_gt), .eq(OKP2));  // open: lt
  hexa_to_7seg hexa_to_7seg_1 (.Hexa(divider_2_out[3:0]), ._7seg(hexa_to_7seg_1__7seg));
  D_Flip_Flop #(.trigger("falling")) d_ff_4 (.Q(d_ff_4_q), .preset(P3), .reset(Reset));  // open: clk, D, Qn, en
  hexa_to_7seg hexa_to_7seg_2 (.Hexa(divider_3_out[3:0]), ._7seg(hexa_to_7seg_2__7seg));
  hexa_to_7seg hexa_to_7seg_3 (.Hexa(divider_1_out[3:0]), ._7seg(hexa_to_7seg_3__7seg));
  D_Flip_Flop #(.trigger("falling")) d_ff_5 (.Q(d_ff_5_q), .preset(P2), .reset(Reset));  // open: clk, D, Qn, en
  Multiplexer #(.width(7)) multiplexer_4 (
    .in0({7{1'b0}}), .in1(hexa_to_7seg_1__7seg), .out(_3rd), .sel(d_ff_4_q));  // open: en
  Multiplexer #(.width(7)) multiplexer_5 (
    .in0({7{1'b0}}), .in1(hexa_to_7seg_2__7seg), .out(_1st), .sel(d_ff_6_q));  // open: en
  D_Flip_Flop #(.trigger("falling")) d_ff_6 (.Q(d_ff_6_q), .preset(P1), .reset(Reset));  // open: clk, D, Qn, en
  Multiplexer #(.width(7)) multiplexer_6 (
    .in0({7{1'b0}}), .in1(hexa_to_7seg_3__7seg), .out(_2nd), .sel(d_ff_5_q));  // open: en
  and and_10 (Exit, OKP1, OKP2, OKP3);

  // Other names for the same wires on the sheet: CLR = Reset
endmodule

module Display_mode (
  input  [6:0] in_1,
  input  [6:0] in_2,
  input  [6:0] in_3,
  input  [6:0] in_4,
  input  Enter,
  input  [3:0] P2,
  output [6:0] out_7,
  output [6:0] out_8,
  output [6:0] out_9,
  output [6:0] out_10,
  output Reset
);

  wire and_2_out, clock_1_out, nor_1_out, or_1_out;
  wire [1:0] not_1_out;
  wire [1:1] comparator_1_eq, comparator_2_eq, comparator_3_eq;
  wire [6:0] multiplexer_1_out, multiplexer_2_out, multiplexer_3_out, multiplexer_4_out, multiplexer_5_out,
       or_2_out;
  wire [27:0] demultiplexer_1_out0, demultiplexer_1_out1;

  Demultiplexer #(.width(28)) demultiplexer_1 (
    .out0(demultiplexer_1_out0), .out1(demultiplexer_1_out1), .in({in_4, in_3, in_2, in_1}), .sel(Enter));  // open: en
  or or_1 (or_1_out, P2[0], P2[1], P2[2], P2[3]);
  and and_1 (Reset, Enter, or_1_out);
  and and_2 (and_2_out, clock_1_out, nor_1_out);
  Clock clock_1 (.out(clock_1_out));
  Comparator #(.width(7)) comparator_1 (
    .a(demultiplexer_1_out1[6:0]), .b(demultiplexer_1_out1[13:7]), .eq(comparator_1_eq[1]));  // open: gt, lt
  Comparator #(.width(7)) comparator_2 (
    .a(demultiplexer_1_out1[6:0]), .b(demultiplexer_1_out1[20:14]), .eq(comparator_2_eq[1]));  // open: gt, lt
  Comparator #(.width(7)) comparator_3 (
    .a(demultiplexer_1_out1[6:0]), .b(demultiplexer_1_out1[27:21]), .eq(comparator_3_eq[1]));  // open: gt, lt
  Multiplexer #(.width(7)) multiplexer_1 (
    .in0({7{1'b0}}), .in1(demultiplexer_1_out1[6:0]), .out(multiplexer_1_out), .sel(and_2_out));  // open: en
  nor nor_1 (nor_1_out, comparator_1_eq[1], comparator_2_eq[1], comparator_3_eq[1]);
  not not_1 (not_1_out[1], nor_1_out);
  Clock #(.highDuration(4), .lowDuration(4)) clock_2 (.out(not_1_out[0]));
  assign or_2_out = multiplexer_1_out | multiplexer_2_out;  // OR_Gate or_2, 7 bits wide
  Multiplexer #(.select(2), .width(7)) multiplexer_2 (
    .in0({7{1'b0}}), .in1({7{1'b0}}), .in2({7{1'b0}}), .in3(demultiplexer_1_out1[6:0]),
    .out(multiplexer_2_out), .sel(not_1_out));  // open: en
  assign out_7 = demultiplexer_1_out0[6:0] | or_2_out;  // OR_Gate or_3, 7 bits wide
  assign out_8 = demultiplexer_1_out0[13:7] | multiplexer_3_out;  // OR_Gate or_4, 7 bits wide
  assign out_9 = demultiplexer_1_out0[20:14] | multiplexer_4_out;  // OR_Gate or_5, 7 bits wide
  assign out_10 = demultiplexer_1_out0[27:21] | multiplexer_5_out;  // OR_Gate or_6, 7 bits wide
  Multiplexer #(.select(2), .width(7)) multiplexer_3 (
    .in0(demultiplexer_1_out1[13:7]), .in1(demultiplexer_1_out1[13:7]), .in2({7{1'b0}}),
    .in3(demultiplexer_1_out1[13:7]), .out(multiplexer_3_out), .sel({comparator_1_eq[1], not_1_out[0]}));  // open: en
  Multiplexer #(.select(2), .width(7)) multiplexer_4 (
    .in0(demultiplexer_1_out1[20:14]), .in1(demultiplexer_1_out1[20:14]), .in2({7{1'b0}}),
    .in3(demultiplexer_1_out1[20:14]), .out(multiplexer_4_out), .sel({comparator_2_eq[1], not_1_out[0]}));  // open: en
  Multiplexer #(.select(2), .width(7)) multiplexer_5 (
    .in0(demultiplexer_1_out1[27:21]), .in1(demultiplexer_1_out1[27:21]), .in2({7{1'b0}}),
    .in3(demultiplexer_1_out1[27:21]), .out(multiplexer_5_out), .sel({comparator_3_eq[1], not_1_out[0]}));  // open: en

  // Notes on the sheet:
  //   Num
  //   1st
  //   2nd
  //   3rd
  //   N
  //   P1
  //   P3
  //   Num
  //   1st
  //   2nd
  //   3rd
endmodule
